# Fritzing sketch wemos_d1_mini (saved by Fritzing 0.9.3b)
breadboards: 1

parts:
  v = AC Power [voltage=220 frequency=60]
  part = DC Power [voltage=5V]
  Hue_Light = LEDs [package=led10mm]
  Wall_switch = SWITCH-MOMENTARY-2 [package=reed_switch_plastic]
  220v_to_5v = Transformer [package=transformer_smd]
  WeMos_D1_Mini1 = WeMos D1 Mini

nets:
  N1: v.V+, 220v_to_5v.1
  N2: part.V+, 220v_to_5v.4, WeMos_D1_Mini1.5V
  N3: part.V-, Wall_switch.2, 220v_to_5v.3, WeMos_D1_Mini1.G
  GND: Hue_Light.C, 220v_to_5v.2
  N4: Wall_switch.1, WeMos_D1_Mini1.D3
